// Digital circuit Half Adder Digital.dig as structural Verilog
module Half_Adder_Digital (
  input  A,
  input  B,
  input  A_2,
  input  B_2,
  input  C
);

  wire and_1_out, and_2_out, xor_1_out, xor_2_out, xor_3_out;

  xor xor_1 (xor_1_out, A, B);
  and and_1 (and_1_out, A, B);
  xor xor_2 (xor_2_out, A_2, B_2);
  and and_2 (and_2_out, A_2, B_2);
  xor xor_3 (xor_3_out, and_2_out, C);
  LED led_1 (.in(xor_1_out));
  LED led_2 (.in(and_1_out));
  LED led_3 (.in(xor_2_out));
  LED led_4 (.in(xor_3_out));
endmodule
